# Fritzing sketch sketch (saved by Fritzing 0.9.3b)
breadboards: 1

parts:
  Part1 = Arduino Uno (Rev3)
  Grove3 = Grove Infrared Receiver
  Grove1 = Grove Infrared Emitter

nets:
  N1: Part1.D2, Grove3.RX
  N2: Part1.D3_PWM, Grove1.TX
  VCC: Part1.5V, Grove3.VCC, Grove1.VCC
  GND: Part1.GND, Grove3.GND, Grove1.GND
